// Logisim project e2449783.circ as structural Verilog: 1 circuit, main circuit main
module main (
  input  A0,
  input  B0,
  input  A1,
  input  B1,
  input  O0,
  input  O1,
  input  O2,
  output L6,
  output L5,
  output L4,
  output L3,
  output L2,
  output L1,
  output L0,
  output S
);

  wire and_1_out, and_2_out, and_3_out, and_4_out, and_5_out, and_6_out, and_7_out, and_8_out, and_9_out,
       and_10_out, and_11_out, and_12_out, and_13_out, and_14_out, and_15_out, and_16_out, and_18_out,
       and_19_out, and_20_out, and_21_out, and_22_out, and_24_out, and_25_out, and_26_out,
       n4_to_1_mux_x2_74153_1_p4, n4_to_1_mux_x2_74153_1_p8, n4_to_1_mux_x2_74153_2_p13,
       n4_to_1_mux_x2_74153_2_p14, n4_to_1_mux_x2_74153_3_p8, not_1_out, not_2_out, not_3_out, not_4_out,
       not_5_out, not_6_out, not_7_out, not_8_out, not_9_out, not_10_out, not_11_out, not_12_out, not_13_out,
       not_14_out, or_1_out, or_2_out, or_3_out, or_4_out, or_5_out, or_6_out, or_7_out, or_8_out, or_9_out,
       or_10_out, or_11_out, or_12_out, or_13_out, or_14_out, xor_1_out, xor_2_out, xor_3_out, xor_4_out,
       xor_5_out, xor_6_out, xor_7_out, xor_8_out, xor_9_out, xor_10_out;

  and and_1 (and_1_out, B0, A0);
  xor xor_1 (xor_1_out, A1, B1);
  xor xor_2 (xor_2_out, B0, A0);
  // _3_to_8_decoder__74138 #(.Facing("east")) 3_to_8_decoder_74138_1: pin names not known; wires that end beside it: O0, O1, O2, 1'b1, 1'b0, 1'b0
  xor xor_3 (xor_3_out, xor_1_out, and_1_out);
  and and_2 (and_2_out, xor_1_out, and_1_out);
  // NOT_Gate not_1 has open pins: in=open, out=not_1_out
  // NOT_Gate not_2 has open pins: in=open, out=not_2_out
  // NOT_Gate not_3 has open pins: in=open, out=not_3_out
  // NOT_Gate not_4 has open pins: in=open, out=not_4_out
  // NOT_Gate not_5 has open pins: in=open, out=not_5_out
  // NOT_Gate not_6 has open pins: in=open, out=not_6_out
  // NOT_Gate not_7 has open pins: in=open, out=not_7_out
  xor xor_4 (xor_4_out, A0, B0);
  xor xor_5 (xor_5_out, A0, A1);
  xor xor_6 (xor_6_out, A1, B1);
  and and_3 (and_3_out, B1, A1);
  xor xor_7 (xor_7_out, B0, B1);
  and and_4 (and_4_out, xor_7_out, and_5_out);
  and and_5 (and_5_out, xor_5_out, xor_6_out);
  not not_8 (not_8_out, xor_6_out);
  and and_6 (and_6_out, xor_2_out, not_1_out);
  and and_7 (and_7_out, xor_3_out, not_1_out);
  xor xor_8 (xor_8_out, and_3_out, and_2_out);
  not not_9 (not_9_out, or_1_out);
  or or_1 (or_1_out, and_4_out, not_8_out);
  and and_8 (and_8_out, xor_8_out, not_1_out);
  xor xor_9 (xor_9_out, B1, A1);
  xor xor_10 (xor_10_out, A0, B0);
  not not_10 (not_10_out, A0);
  and and_9 (and_9_out, B0, A0);
  or or_2 (or_2_out, B0, B1);
  and and_10 (and_10_out, xor_10_out, not_5_out);
  and and_11 (and_11_out, xor_9_out, not_5_out);
  and and_12 (and_12_out, xor_4_out, not_2_out);
  and and_13 (and_13_out, not_9_out, not_2_out);
  not not_11 (not_11_out, B0);
  and and_14 (and_14_out, B1, A1);
  and and_15 (and_15_out, not_6_out, and_9_out);
  and and_16 (and_16_out, and_14_out, not_6_out);
  // _4_to_1_MUX__x2___74153 #(.Facing("east")) 4_to_1_mux_x2_74153_1: pin names not known; wires that end beside it: 1'b1, or_2_out, B1, n4_to_1_mux_x2_74153_1_p4, 1'b0, A0, A1, n4_to_1_mux_x2_74153_1_p8
  and and_17 (n4_to_1_mux_x2_74153_1_p4, B0, B1);
  not not_12 (not_12_out, A1);
  and and_18 (and_18_out, not_11_out, not_10_out);
  not not_13 (not_13_out, B1);
  and and_19 (and_19_out, not_13_out, not_12_out);
  and and_20 (and_20_out, not_7_out, and_18_out);
  and and_21 (and_21_out, and_19_out, not_7_out);
  and and_22 (and_22_out, n4_to_1_mux_x2_74153_1_p8, not_4_out);
  not not_14 (not_14_out, n4_to_1_mux_x2_74153_1_p8);
  and and_23 (S, not_14_out, not_2_out);
  or or_3 (or_3_out, and_20_out, and_15_out);
  or or_4 (or_4_out, and_21_out, and_16_out);
  or or_5 (or_5_out, or_4_out, and_7_out);
  or or_6 (or_6_out, or_3_out, and_6_out);
  or or_7 (or_7_out, or_6_out, and_12_out);
  or or_8 (or_8_out, or_5_out, and_13_out);
  or or_9 (or_9_out, or_8_out, and_11_out);
  or or_10 (or_10_out, or_9_out, and_26_out);
  or or_11 (or_11_out, or_7_out, and_22_out);
  or or_12 (or_12_out, or_11_out, and_10_out);
  or or_13 (or_13_out, or_12_out, and_25_out);
  or or_14 (or_14_out, and_24_out, and_8_out);
  // _4_to_1_MUX__x2___74153 #(.Facing("east")) 4_to_1_mux_x2_74153_2: pin names not known; wires that end beside it: B0, 1'b0, 1'b0, 1'b0, B1, B0, 1'b0, 1'b0, 1'b0, A0, 1'b0, A1, n4_to_1_mux_x2_74153_2_p13, n4_to_1_mux_x2_74153_2_p14
  // _4_to_1_MUX__x2___74153 #(.Facing("east")) 4_to_1_mux_x2_74153_3: pin names not known; wires that end beside it: 1'b0, B1, B0, 1'b0, 1'b0, A0, A1, n4_to_1_mux_x2_74153_3_p8
  // _3_to_8_decoder__74138 #(.Facing("east")) 3_to_8_decoder_74138_2: pin names not known; wires that end beside it: or_13_out, or_10_out, or_14_out, 1'b1, 1'b0, 1'b0, L4
  and and_24 (and_24_out, not_3_out, n4_to_1_mux_x2_74153_3_p8);
  and and_25 (and_25_out, n4_to_1_mux_x2_74153_2_p13, not_3_out);
  and and_26 (and_26_out, n4_to_1_mux_x2_74153_2_p14, not_3_out);
  // NOT_Gate not_15 has open pins: in=open, out=L0
  // NOT_Gate not_16 has open pins: in=open, out=L1
  // NOT_Gate not_17 has open pins: in=open, out=L2
  // NOT_Gate not_18 has open pins: in=open, out=L3
  // NOT_Gate not_19 has open pins: in=open, out=L4
  // NOT_Gate not_20 has open pins: in=open, out=L5
  // NOT_Gate not_21 has open pins: in=open, out=L6

  // Notes on the sheet:
  //   A+B
  //   A XOR B
  //   A . B
  //   (AVB)'
  //   B>=A
  //   B0
  //   B1
  //   B2
endmodule
